# Fritzing sketch connection (saved by Fritzing 0.9.6b)
breadboards: 2

parts:
  Part1 = Arduino Uno (Rev3)
  Part2 = Soil Moisture Sensor
  Part3 = Soil Moisture Sensor
  Part5 = Soil Moisture Sensor
  Part4 = Soil Moisture Sensor
  LCD1 = LCD screen [part_number="1602 display"]
  U1 = POT [package=pot_alpha_rv16af-20]
  Part6 = Humidity Temperature Sensor SHT15 [part_number="Temp and humidity sensor"]

nets:
  N1: Part1.A0, Part2.SIG
  N2: Part1.A1, Part5.SIG
  N3: Part1.A2, Part4.SIG
  N4: Part1.A3, Part3.SIG
  N5: Part1.D8, LCD1.LED+
  N6: Part1.D9_PWM, LCD1.RS
  N7: Part1.D10_PWM/SS, LCD1.E
  GND: Part1.GND, Part2.GND, Part3.GND, Part5.GND, Part4.GND, Part6.GND
  N8: Part1.A4/SDA, Part6.SCL
  N9: Part1.A5/SCL, Part6.SDA
  N10: Part1.D4, LCD1.DB4
  N11: Part1.D5_PWM, LCD1.DB5
  N12: Part1.D6_PWM, LCD1.DB6
  N13: Part1.D7, LCD1.DB7
  VCC: Part1.5V, Part2.VCC, Part3.VCC, Part5.VCC, Part6.VCC
  N14: LCD1.VSS, LCD1.LED-, U1.E
  N15: LCD1.VDD, LCD1.R/W, U1.A
  N16: LCD1.V0, U1.S
